# Fritzing sketch Wiring Diagram (saved by Fritzing 0.9.3b)
breadboards: 1

parts:
  Part1 = Arduino Uno (Rev3)
  R1 = Rotary Potentiometer (Large) [maximum_resistance=100kΩ package=THT]
  R2 = Rotary Potentiometer (Large) [maximum_resistance=100kΩ package=THT]
  R3 = Rotary Potentiometer (Large) [maximum_resistance=100kΩ package=THT]
  R4 = Rotary Potentiometer (Large) [maximum_resistance=100kΩ package=THT]
  J1 = Basic Servo

nets:
  N1: Part1.A1, R1.wiper
  N2: Part1.A2, R4.wiper
  N3: Part1.A3, R3.wiper
  N4: Part1.A4/SDA, R2.wiper
  N5: Part1.D13/SCK, J1.pulse
  5V: Part1.5V, R1.leg2, R2.leg2, R3.leg2, R4.leg2, J1.vcc
  GND: Part1.GND, R1.leg1, R2.leg1, R3.leg1, R4.leg1, J1.gnd
